// Logisim project isatrabalho.circ as structural Verilog
module registradores (
  input  r31,
  input  [31:0] in_2,
  input  rs2,
  input  rd
);

  Register #(.width(32)) r1 ();  // open: D, en, clk, Q, clr
  Register #(.width(32)) r2 ();  // open: D, en, clk, Q, clr
  Register #(.width(32)) r3 ();  // open: D, en, clk, Q, clr
  Register #(.width(32)) r4 ();  // open: D, en, clk, Q, clr
  Register #(.width(32)) r5 ();  // open: D, en, clk, Q, clr
  Register #(.width(32)) r6 ();  // open: D, en, clk, Q, clr
  Register #(.width(32)) r7 ();  // open: D, en, clk, Q, clr
endmodule
